# Fritzing sketch circuit24 (saved by Fritzing 0.9.1b)
breadboards: 1

parts:
  Composant1 = Arduino Nano (Rev3.0)
  M1 = DC Motor
  IC1 = L293D [package=THT]
  Part2 = Bluetooth HC-05 Macho
  Part3 = Bluetooth HC-05 Macho
  M2 = DC Motor
  VCC1 = 4 x AAA Battery Mount
  R1 = Resistor [tolerance=±5% resistance=2k package=THT]
  R2 = Resistor [tolerance=±5% resistance=1k package=THT]
  R3 = Resistor [tolerance=±5% resistance=2k package=THT]
  R4 = Resistor [tolerance=±5% resistance=1k package=THT]

nets:
  GND: Composant1.GND, IC1.0V, Part2.GND, Part3.GND, VCC1.-, R1.Pin_0, R3.Pin_0
  N1: Composant1.D2, IC1.In_3
  N2: Composant1.D3, IC1.In_4
  N3: Composant1.D4, IC1.In_2
  N4: Composant1.D5, IC1.In_1
  N5: Composant1.D9, IC1.Enable_1
  N6: Composant1.D10, IC1.Enable_2
  VCC: Composant1.5V, Part2.VCC, Part3.VCC
  N7: Composant1.A3, R4.Pin_1
  N8: Composant1.A2, Part2.TXD
  N9: Composant1.A1, R2.Pin_1
  N10: Composant1.A0, Part3.TXD
  N11: M1.pin_1, IC1.Out_2_(_Controlled_by_Enable_1_)
  N12: M1.pin_2, IC1.Out_1_(_Controlled_by_Enable_1_)
  N13: IC1.+Vmotor, IC1.+V, VCC1.+
  N14: IC1.Out_3_(_Controlled_by_Enable_2_), M2.pin_2
  N15: IC1.Out_4_(_Controlled_by_Enable_2_), M2.pin_1
  N16: Part2.RXD, R3.Pin_1, R4.Pin_0
  N17: Part3.RXD, R1.Pin_1, R2.Pin_0
